# Fritzing sketch Midterm Fritz V2 (saved by Fritzing 1.0.4)
breadboards: 1

parts:
  A1 = Particle - Photon2
  U1 = ENCODER_RGB [package=encoder_led_2]
  C1 = Electrolytic Capacitor [capacitance=10μF voltage=35V package="0605 [SMD, electrolytic]"]
  M1 = BMP280
  OLED_I2C1 = OLED 128x64 I2C Monochrome Display

nets:
  GND: A1.Pin_2, A1.Pin_4, A1.Pin_30, A1.Pin_31, A1.Pin_32, U1.C, U1.+, C1.-, M1.GND, OLED_I2C1.GND
  N1: A1.Pin_13, C1.+
  N2: A1.Pin_14, U1.A
  N3: A1.Pin_15, U1.B#2
  N4: A1.Pin_17, M1.SDA, OLED_I2C1.SDA
  N5: A1.Pin_18, M1.SCL, OLED_I2C1.SCK
  VIN: M1.VIN, OLED_I2C1.VDD

custom parts:
  Particle - Photon2: The Photon 2 is a microcontroller and Wi-Fi networking developed by particle. Features: 802.11a/b/g/n Wi-Fi, 2.4 GHz and 5 GHz Integrated PCB antenna Integrated U.FL connector for external antenna Integrated RF switch BLE 5 using same antenna as Wi-Fi Realtek RTL8721DM MCU ARM Cortex M33 CPU, 200 MHz 2048 KB (2 MB) user application maximum size 3072 KB (3 MB) of RAM available to user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
  ENCODER_RGB: SparkFun RGB rotary Encoder
  BMP280: Temperature Humidity Barometric presure Sensor, I2C
